# Fritzing sketch AD-2000M_Wemos (saved by Fritzing 0.9.3b)
circuit board: 5.4989cm x 6.19959cm

parts:
  WeMos_D1_Mini1 = WeMos D1 Mini
  R1 = Resistor [tolerance=±5% resistance=10k package=THT]
  R2 = Resistor [tolerance=±5% resistance=10k package=THT]
  J2 = screw terminal, 7 pins
  Power_plug1 = Power plug [part_number=12V]
  IC1 = Voltage Regulator [package=to-220-alt]
  C1 = Electrolytic Capacitor [capacitance=1mF package="100 mil [THT, electrolytic]"]
  C2 = Electrolytic Capacitor [capacitance=0.1mF package="100 mil [THT, electrolytic]"]
  R3 = Resistor [tolerance=±5% resistance=330 package=THT]
  LED1 = LED - 5mm [color="Red (633nm)" package="5 mm [THT]"]
  C3 = Ceramic Capacitor [capacitance=0.1µF package="100 mil [THT, multilayer]"]
  Q1 = MOSFET-NCHANNEL [package=to220v]
  R4 = Resistor [tolerance=±5% resistance=10k package=THT]
  D1 = Rectifier Diode [part_number=1N4001 package="300 mil [THT]"]
  J3 = Screw terminal - 2 pins [package=THT]
  GY-21P = female pin header, 4 pins [form="♀ (female)"]
  J4 = Screw terminal - 2 pins [package=THT]

nets:
  N1: WeMos_D1_Mini1.3V3, GY-21P.pin1
  N2: WeMos_D1_Mini1.5V, R1.Pin_0, R2.Pin_0, IC1.OUT, C2.+, R3.Pin_0, C3.1
  N3: WeMos_D1_Mini1.D1, J2.pin5
  N4: WeMos_D1_Mini1.D2, J2.pin4
  N5: WeMos_D1_Mini1.D3, R2.Pin_1, J2.pin3
  N6: WeMos_D1_Mini1.D4, R1.Pin_1, J2.pin6
  N7: WeMos_D1_Mini1.D6, GY-21P.pin4
  N8: WeMos_D1_Mini1.D7, GY-21P.pin3
  N9: WeMos_D1_Mini1.D8, Q1.G, R4.Pin_0
  GND: WeMos_D1_Mini1.G, J2.pin2, J2.pin7, Power_plug1.GND, IC1.GND, C1.-, C2.-, LED1.cathode, C3.0, Q1.S, R4.Pin_1, GY-21P.pin2, J4.pin1
  +12V: J2.pin1, Power_plug1.VCC, IC1.IN, C1.+, D1.cathode, J3.pin1, J4.pin2
  N10: R3.Pin_1, LED1.anode
  N11: Q1.D, D1.anode, J3.pin2

notes:
  12V
  GND
  PUSH
  NC
  BELL1
  BELL2
  D0
  D1
  +12V
  D0 (WIEGAND)
  D1 (WIEGAND)
  BELL 1
  BELL 2
  To electric lock
  AD-2000M RFID
  PSH
  BL1
  BL2
  -
  +
  Q
  S
